# Fritzing sketch Gradient_Mixer_05.07.2021 (saved by Fritzing 0.8.7b)
circuit board: 10.6588cm x 5.35731cm
breadboards: 1

parts:
  R1 = Resistor [tolerance=±5% resistance=1k package=THT]
  Q1 = NPN-Transistor [package="TO92 [THT]"]
  R5 = Resistor [tolerance=±5% resistance=1k package=THT]
  R6 = Resistor [tolerance=±5% resistance=1k package=THT]
  Antenna = RF-LINK_TX [package=rf-link_tx]
  R7 = Resistor [tolerance=±5% resistance=100 package=THT]
  R2 = Resistor [tolerance=±5% resistance=1k package=THT]
  12V_INPUT = LITTLEBITS_FEMALE [package=little_bits_female]
  D1 = Diode [package=diode-1n4001]
  D2 = Diode [package=diode-1n4001]
  Stop_Button = LITTLEBITS_FEMALE [package=little_bits_female]
  Play_Button = LITTLEBITS_FEMALE [package=little_bits_female]
  Solenoid_Valve_OUTPUT = LITTLEBITS_MALE [package=little_bits_male]
  LED = LITTLEBITS_MALE [package=little_bits_male]
  Arduino_Mega = Arduino Mega 2560 (Rev3)

nets:
  N1: R1.Pin_0, Stop_Button.GND, Arduino_Mega.D20/SDA, Arduino_Mega.SDA
  GND: R1.Pin_1, Antenna.GND, R7.Pin_0, R2.Pin_1, Arduino_Mega.GND
  N2: Q1.E, 12V_INPUT.GND
  N3: Q1.B, R5.Pin_1
  N4: Q1.C, R6.Pin_0, D2.A, Solenoid_Valve_OUTPUT.GND
  N5: R5.Pin_0, D1.C
  N6: R6.Pin_1, 12V_INPUT.VCC, D2.C, Solenoid_Valve_OUTPUT.SIG
  N7: Antenna.DATA, Arduino_Mega.D10_PWM
  N8: Antenna.+5V, Arduino_Mega.D9_PWM
  N9: R7.Pin_1, LED.GND
  N10: R2.Pin_0, Play_Button.GND, Arduino_Mega.D21/SCL, Arduino_Mega.SCL
  N11: D1.A, Arduino_Mega.D8_PWM
  VCC: Stop_Button.VCC, Play_Button.VCC, Arduino_Mega.D19/RX1
  N12: LED.VCC, Arduino_Mega.D18/TX1

// code stored in the sketch: arduinocomponenttester.ino
#include <RCSwitch.h>
RCSwitch mySwitch = RCSwitch();

// Pins for Stop Buttons                                 
const int StopLED = 19;
const int StopButton = 21;
const int PlayButton = 14;

const int VALVE = 8;

// variables will change:
volatile int buttonState = 0;         // variable for reading the pushbutton status

void setup() {
  Serial.begin(9600);

  pinMode(9, OUTPUT);
  digitalWrite(9, HIGH); //POWER ANTENNA
  // Transmitter is connected to Arduino Pin #10  
  mySwitch.enableTransmit(10);

  // Optional set pulse length.
  mySwitch.setPulseLength(718);
  
  // Optional set protocol (default is 1, will work for most outlets)
  mySwitch.setProtocol(2);

  // Optional set number of transmission repetitions.
  mySwitch.setRepeatTransmit(2);

  //pinMode(12, OUTPUT);
  //
  digitalWrite(12, LOW); 

  pinMode(VALVE, OUTPUT);
  
  
  pinMode(StopLED, OUTPUT);
  
  pinMode(StopButton,INPUT);
  pinMode(PlayButton, INPUT);
  
  // Attach an interrupt to the ISR vector
  attachInterrupt(digitalPinToInterrupt(StopButton), PauseProgram,  RISING);
}

void loop() {
  // put your main code here, to run repeatedly:
  digitalWrite(VALVE, LOW);
  //mySwitch.send("10101110000010000101111000000000");
  digitalWrite(StopLED, LOW);
  delay(5);
  
  digitalWrite(VALVE, HIGH);
  //mySwitch.send("10100110000010000101111000000000");
  digitalWrite(StopLED, HIGH);
  delay(5);
}

void PauseProgram(){
  //if (currentPage == '5'){
    int decider = 1;

//    pump = 0;
    mySwitch.send("10101110000010000101111000000000");
    digitalWrite(StopLED, HIGH);
    
    //Wait until Play Button is pressed
    while(decider == 1){
      buttonState = digitalRead(PlayButton);
      if (buttonState == HIGH){
        decider = 0;
        //Turns Pump ON
        //  pump = 1;
        mySwitch.send("10100110000010000101111000000000");
      digitalWrite(StopLED, LOW);
  
      }
    }
  //}
}
